# Fritzing sketch 3 LEDs en paralelo (saved by Fritzing 0.9.3b)
breadboards: 1

parts:
  VCC1 = Battery
  LED1 = LED - 5mm [color="Red (633nm)" package="5 mm [THT]"]
  LED2 = LED - 5mm [color="Red (633nm)" package="5 mm [THT]"]
  LED3 = LED - 5mm [color="Red (633nm)" package="5 mm [THT]"]

nets:
  N1: VCC1.-, LED1.cathode, LED2.cathode, LED3.cathode
  N2: VCC1.+, LED1.anode, LED2.anode, LED3.anode
