# Fritzing sketch 3 LEDs en serie (saved by Fritzing 0.9.3b)
breadboards: 1

parts:
  VCC1 = Battery
  R1 = Resistor [tolerance=±5% resistance=220 package="1206 [SMD]"]
  R2 = Resistor [tolerance=±5% resistance=220 package="1206 [SMD]"]
  R3 = Resistor [tolerance=±5% resistance=220 package="1206 [SMD]"]
  LED1 = LED - 5mm [color="Red (633nm)" package="5 mm [THT]"]
  LED2 = LED - 5mm [color="Red (633nm)" package="5 mm [THT]"]
  LED3 = LED - 5mm [color="Red (633nm)" package="5 mm [THT]"]

nets:
  N1: VCC1.-, R1.Pin_0, R2.Pin_0, R3.Pin_0
  N2: VCC1.+, LED1.anode, LED2.anode, LED3.anode
  N3: R1.Pin_1, LED1.cathode
  N4: R2.Pin_1, LED2.cathode
  N5: R3.Pin_1, LED3.cathode
