# Fritzing sketch Led y pulsador (saved by Fritzing 0.9.3b)
breadboards: 1

parts:
  U1 = LIPO-110mAh [package=lipo-110]
  R1 = Resistor [tolerance=±5% resistance=220 package=THT]
  LED2 = LED - 5mm [color="Red (633nm)" package="5 mm [THT]"]
  S1 = Momentary Switch [package=ksa_sealed_tac_switch]

nets:
  N1: U1.+, S1.3, S1.4
  N2: U1.-, LED2.cathode
  N3: R1.Pin_0, S1.1, S1.2
  N4: R1.Pin_1, LED2.anode
