# Fritzing sketch Led con LDR (saved by Fritzing 0.9.3b)
breadboards: 1

parts:
  VCC1 = Battery block 9V
  R1 = PHOTOCELL [package=photocell]
  Q1 = NPN-Transistor [package="SOT-23 [SMD]"]
  R2 = Resistor [tolerance=±5% resistance=220 package=THT]
  LED1 = LED - 5mm [color="Red (633nm)" package="5 mm [THT]"]
  R3 = Resistor [tolerance=±5% resistance=120k package=THT]

nets:
  N1: VCC1.-, R1.P$1, Q1.2
  N2: VCC1.+, R2.Pin_0, R3.Pin_0
  N3: R1.P$2, Q1.0, R3.Pin_1
  N4: Q1.1, R2.Pin_1, LED1.anode
