# Fritzing sketch Led con interruptor (saved by Fritzing 0.9.3b)
breadboards: 1

parts:
  VCC1 = Battery block 9V
  R1 = Resistor [tolerance=±0.05% resistance=220 package="0805 [SMD]"]
  S1 = Pushbutton [package="[THT]"]
  LED1 = LED - 5mm [color="Red (633nm)" package="5 mm [THT]"]

nets:
  N1: VCC1.-, LED1.cathode
  N2: VCC1.+, R1.Pin_0
  N3: R1.Pin_1, S1.Pin_3, S1.Pin_4
  N4: S1.Pin_1, S1.Pin_2, LED1.anode
