# Fritzing sketch Motor y Led (saved by Fritzing 0.9.3b)
breadboards: 1

parts:
  VCC1 = Battery
  M1 = DC Motor
  LED1 = LED - 5mm [color="Red (633nm)" package="5 mm [THT]"]

nets:
  N1: VCC1.-, M1.pin_1, LED1.cathode
  N2: VCC1.+, M1.pin_2, LED1.anode
