# Fritzing sketch Velocidad de motor DC con transistor y potenciómetro (saved by Fritzing 0.9.3b)
breadboards: 1

parts:
  R1 = Resistor [tolerance=±5% resistance=330 package=THT]
  VCC1 = Battery block 9V
  LED1 = LED - 5mm [color="Red (633nm)" package="5 mm [THT]"]
  M1 = DC Motor
  U1 = POT [package=alps_pot]
  Q1 = NPN-Transistor [package="SOT-23 [SMD]"]

nets:
  N1: R1.Pin_0, VCC1.-, M1.pin_1
  N2: R1.Pin_1, LED1.cathode
  N3: VCC1.+, U1.A, Q1.1
  N4: LED1.anode, U1.S, Q1.0
  N5: M1.pin_2, U1.E, Q1.2
