# Fritzing sketch Práctica de evaluación - 3 LEDs en serie con pulsador (saved by Fritzing 0.9.3b)
breadboards: 1

parts:
  VCC1 = Battery block 9V
  LED3 = LED - 5mm [color="Red (633nm)" package="5 mm [THT]"]
  LED4 = LED - 5mm [color="Red (633nm)" package="5 mm [THT]"]
  LED5 = LED - 5mm [color="Red (633nm)" package="5 mm [THT]"]
  R1 = Resistor [tolerance=±5% resistance=220 package=THT]
  S1 = Pushbutton [package="[THT]"]

nets:
  N1: VCC1.-, LED3.cathode
  N2: VCC1.+, S1.Pin_3, S1.Pin_4
  N3: LED3.anode, LED4.cathode
  N4: LED4.anode, LED5.cathode
  N5: LED5.anode, R1.Pin_0
  N6: R1.Pin_1, S1.Pin_1, S1.Pin_2
