# Fritzing sketch 3 LEDs en paralelo (saved by Fritzing 0.9.3b)
breadboards: 1

parts:
  LED1 = LED - 5mm [color="Red (633nm)" package="5 mm [THT]"]
  LED2 = LED - 5mm [color="Red (633nm)" package="5 mm [THT]"]
  LED3 = LED - 5mm [color="Red (633nm)" package="5 mm [THT]"]
  R1 = Resistor [tolerance=±5% resistance=220 package=THT]
  U1 = LIPO-1000mAh [package=lipo-1000]

nets:
  N1: LED1.cathode, LED2.cathode, LED3.cathode, U1.-
  N2: LED1.anode, LED2.anode, LED3.anode, R1.Pin_1
  N3: R1.Pin_0, U1.+
