# Fritzing sketch Arduino UNO - LED con R220 (saved by Fritzing 0.9.3b)
breadboards: 1

parts:
  R1 = Resistor [tolerance=±5% resistance=220 package=THT]
  LED1 = LED - 5mm [color="Red (633nm)" package="5 mm [THT]"]
  part = Arduino Uno (Rev3)

nets:
  N1: R1.Pin_0, part.D13/SCK
  N2: R1.Pin_1, LED1.anode
  N3: LED1.cathode, part.GND
