# Fritzing sketch CNC (saved by Fritzing 0.9.3b)

parts:
  Componente1 = Arduino Uno (Rev3)  # not connected
  Arduino_CNC_Shield_V3_00_1 = Arduino_CNC_V3.00
  M1 = Stepper Motor - Bipolar
  M2 = Stepper Motor - Bipolar
  J1 = Basic Servo

nets:
  N1: Arduino_CNC_Shield_V3_00_1.X-MTR_'1', M2.A
  N2: Arduino_CNC_Shield_V3_00_1.X-MTR_'2', M2.C
  N3: Arduino_CNC_Shield_V3_00_1.X-MTR_'3', M2.B
  N4: Arduino_CNC_Shield_V3_00_1.X-MTR_'4', M2.D
  N5: Arduino_CNC_Shield_V3_00_1.Y-MTR_'1', M1.A
  N6: Arduino_CNC_Shield_V3_00_1.Y-MTR_'2', M1.C
  N7: Arduino_CNC_Shield_V3_00_1.Y-MTR_'3', M1.B
  N8: Arduino_CNC_Shield_V3_00_1.Y-MTR_'4', M1.D
  N9: Arduino_CNC_Shield_V3_00_1.5V, J1.pulse
  GND: Arduino_CNC_Shield_V3_00_1.GND, J1.gnd
  N10: Arduino_CNC_Shield_V3_00_1.End_Stops_Z+_(and_Z-)_/_SpnEn, J1.vcc

custom parts:
  Arduino_CNC_V3.00: Protoneer Arduino CNC Shield V3.00 If using Grbl V0.9: The “A” axis can not be used (yet). The “SCL” (Arduino A5) pin is now used for 'Probing' input. The “End Stops Z+ & Z-” (Arduino D11) and “SpnEn” (Arduino D12) have been switched!
